# Fritzing sketch tour-sign (saved by Fritzing 0.9.2b)

parts:
  Part1 = Arduino Pro Mini v13
  7SEG1 = 7-Segment LED I2C Backpack (white)
  S1 = Toggle Switch [package=THT]
  Power_plug1 = Power plug

nets:
  N1: Part1.A4, 7SEG1.SCL
  N2: Part1.A5, 7SEG1.SDA
  N3: Part1.RAW, S1.L1
  GND: Part1.GND, 7SEG1.GND, Power_plug1.GND
  N4: Part1.VCC, 7SEG1.V+
  N5: S1.COM, Power_plug1.VCC

custom parts:
  7-Segment LED I2C Backpack (white): 4-digit, 7-segment LED Display with I2C Control
